# Fritzing sketch gamepad_with_3_buttons (saved by Fritzing 0.9.3b)
breadboards: 1

parts:
  S2 = Round Pushbutton
  R2 = Resistor [tolerance=±5% resistance=220 package="0805 [SMD]"]
  Bauteil1 = ESP32 Module Testbed  # not connected
  S4 = Round Pushbutton
  R3 = Resistor [tolerance=±5% resistance=22k package="0805 [SMD]"]
  R4 = Resistor [tolerance=±5% resistance=22k package="0805 [SMD]"]
  LED3 = RGB LED (com. cathode, rbg) [package="5 mm [THT]"]

nets:
  N1: S2.leg0, S4.leg0
  N2: S2.leg1, R4.Pin_1
  N3: R2.Pin_0, LED3.common_cathode
  N4: S4.leg1, R3.Pin_1
  N5: R3.Pin_0, R4.Pin_0

custom parts:
  ESP32 Module Testbed: The ESP32 Module Testbed is a breadboard compatible breakout board for the ESP-WROOM-03 ESP32 module. The ESP32 is a WiFi and Bluetooth-enabled 32-bit, dual-core microcontroller.
